# Fritzing sketch wildcat (saved by Fritzing 0.9.3b)
circuit board: 8.46667cm x 5.64444cm
breadboards: 1

parts:
  Part1 = Adafruit Feather HUZZAH ESP8266 [part_number="Adafruit #2821"]
  S3 = Momentary Switch [package=ksa_sealed_tac_switch]
  Part2 = Adafruit 8x16 LED Matrix FeatherWing - Red [part_number="Adafruit #3152"]  # not connected

nets:
  N1: Part1.GND, S3.1
  N2: Part1.GPIO2, S3.3

notes:
  The 16x8 LED featherwing fits on top of the feather huzzah when in use.
  I've only placed it to one side here to show the huzzah on the diagram.

custom parts:
  Adafruit Feather HUZZAH ESP8266: his is the Adafruit Feather HUZZAH ESP8266 - our take on an 'all-in-one' ESP8266 WiFi development board with built in USB and battery charging. Its an ESP8266 WiFi module with all the extras you need, ready to rock! We have other boards in the Feather family, check'em out here. At the Feather HUZZAH's heart is an ESP8266 WiFi microcontroller clocked at 80 MHz and at 3.3V logic. This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
  Adafruit 8x16 LED Matrix FeatherWing - Red: You will chirp with delight when you see how easy it is to make your very own 8x16 LED matrix display for any Feather. This kit combines two of our adorable miniature LED matrices with a FeatherWing driver board. At 0.8" square, these little 8x8 matrices have got everything a big LED matrix has, but bite sized! Double them up for 128 total bright red LEDs. This is the Red Adafruit 0.8" 8x16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
